# Fritzing sketch George (saved by Fritzing 0.9.4)
breadboards: 1

parts:
  LED1 = LED - 5mm [color="Red (633nm)" package="5 mm [THT]"]
  LED2 = LED - 5mm [color="Red (633nm)" package="5 mm [THT]"]
  Bluno_Nano1 = Arduino Nano (Rev3.0)
  Mic1 = KY-038  # not connected

nets:
  N1: LED1.cathode, LED2.cathode, Bluno_Nano1.GND

custom parts:
  KY-038: ky-038 Microphone sound sensor module
