# Fritzing sketch StarWarsDiorama (saved by Fritzing 0.9.4)
breadboards: 1

parts:
  U1 = ESP8266 NodeMCU LoLin module
  LED2 = smd LED [color="Green (555nm)" package="0603 [SMD]"]
  LED3 = smd LED [color="White (6500K)" package="0603 [SMD]"]
  LED4 = smd LED [color="White (6500K)" package="0603 [SMD]"]
  R1 = Resistor [tolerance=±5% resistance=220 package="0805 [SMD]"]
  R2 = Resistor [tolerance=±5% resistance=220 package="2512 [SMD]"]
  R3 = Resistor [tolerance=±5% resistance=220 package="2010 [SMD]"]
  R4 = Resistor [tolerance=±5% resistance=220 package="2010 [SMD]"]
  LED5 = LED - 5mm [color="Red (633nm)" package="5 mm [THT]"]

nets:
  N1: U1.D0, LED2.cathode
  N2: U1.D1, LED5.cathode
  N3: U1.3V3, R1.Pin_0, R2.Pin_0, R3.Pin_0, R4.Pin_0
  N4: U1.D5, LED3.cathode
  N5: U1.D8, LED4.cathode
  N6: LED2.anode, R1.Pin_1
  N7: LED3.anode, R3.Pin_1
  N8: LED4.anode, R4.Pin_1
  N9: R2.Pin_1, LED5.anode

notes:
  Use approximations for the LEDS and resistors to start with.

custom parts:
  ESP8266 NodeMCU LoLin module: ESP8266 based NodeMCU
